# Fritzing sketch bme280spi (saved by Fritzing 0.9.3b)
breadboards: 1

parts:
  BME280_(SPI1) = BME280 Breakout
  STM32_Blue_Pill = STM32F103C8T6 blue mini board
  BME280_(SPI2) = BME280 Breakout

nets:
  N1: BME280_(SPI1).!CS, STM32_Blue_Pill.B6
  N2: BME280_(SPI1).SDI/SDA, STM32_Blue_Pill.B9
  N3: BME280_(SPI1).SDO/ADR, STM32_Blue_Pill.B8
  N4: BME280_(SPI1).SCK/SCL, STM32_Blue_Pill.B7
  3.3V: BME280_(SPI1).3.3V, STM32_Blue_Pill.A12, BME280_(SPI2).3.3V
  GND: BME280_(SPI1).GND, STM32_Blue_Pill.A11, BME280_(SPI2).GND
  N5: STM32_Blue_Pill.G, STM32_Blue_Pill.VBAT, STM32_Blue_Pill.GND
  N6: STM32_Blue_Pill.A0, BME280_(SPI2).!CS
  N7: STM32_Blue_Pill.A1, BME280_(SPI2).SCK/SCL
  N8: STM32_Blue_Pill.A2, BME280_(SPI2).SDO/ADR
  N9: STM32_Blue_Pill.A3, BME280_(SPI2).SDI/SDA
  N10: STM32_Blue_Pill.3.3V, STM32_Blue_Pill.3.3

notes:
  SPI1
  SPI2
